# Fritzing sketch I2C_pcf8574 (saved by Fritzing 0.9.2b)
stripboards: 1

parts:
  U1 = PCF8574 [package="DIP16 [THT]"]
  J1 = Screw terminal - 2 pins [package=THT]
  J2 = Screw terminal - 2 pins [package=THT]
  R2 = Resistor [tolerance=±5% resistance=10k package=THT]
  R1 = Resistor [tolerance=±5% resistance=10k package=THT]
  J3 = female pin header, 3 pins [form="♀ (female)"]
  J4 = female pin header, 3 pins [form="♀ (female)"]
  R3 = Resistor [tolerance=±5% resistance=10k package=THT]
  R4 = Resistor [tolerance=±5% resistance=10k package=THT]
  R5 = Resistor [tolerance=±5% resistance=10k package=THT]
  J5 = female pin header, 8 pins [form="♀ (female)"]

nets:
  N1: U1.A0, J4.pin1, R3.Pin_0
  N2: U1.A1, J4.pin2, R4.Pin_0
  N3: U1.A3, J4.pin3, R5.Pin_0
  N4: U1.P0, J5.pin1
  N5: U1.P1, J5.pin2
  N6: U1.P2, J5.pin3
  N7: U1.P3, J5.pin4
  N8: U1.GND, J1.pin2, J3.pin1, J3.pin2, J3.pin3
  N9: U1.P4, J5.pin8
  N10: U1.P5, J5.pin7
  N11: U1.P6, J5.pin6
  N12: U1.P7, J5.pin5
  N13: U1.SCL, J2.pin2, R2.Pin_0
  N14: U1.SDA, J2.pin1, R1.Pin_0
  N15: U1.VCC, J1.pin1, R2.Pin_1, R1.Pin_1, R3.Pin_1, R4.Pin_1, R5.Pin_1

notes:
  SDA SCL
  5V GND
  Key Pin 1
