# Fritzing sketch baseBoard1284_new (saved by Fritzing 0.9.3b)
stripboards: 1

parts:
  R6 = Resistor [tolerance=±5% resistance=10k package=THT]
  S2 = Pushbutton [package="[THT]"]
  R7 = Resistor [tolerance=±5% resistance=220 package=THT]
  R8 = Resistor [tolerance=±5% resistance=220 package=THT]
  R9 = Resistor [tolerance=±5% resistance=220 package=THT]
  C6 = Ceramic Capacitor [capacitance=100nF package="100 mil [THT, multilayer]"]
  C7 = Ceramic Capacitor [capacitance=100nF package="100 mil [THT, multilayer]"]
  XTAL2 = Crystal [frequency="16 Mhz" package=THT]
  C8 = Ceramic Capacitor [capacitance=22pF package="100 mil [THT, multilayer]"]
  C9 = Ceramic Capacitor [capacitance=22pF package="100 mil [THT, multilayer]"]
  Atmega2 = ATmega644 [package=pdpi]
  J3 = Screw terminal - 2 pins [package=THT]
  J4 = Screw terminal - 2 pins [package=THT]
  J_FTDI1 = female pin header, 5 pins [form="♀ (female)"]
  J5 = Screw terminal - 2 pins [package=THT]
  C10 = Ceramic Capacitor [capacitance=100nF package="100 mil [THT, multilayer]"]
  Q2 = NPN-Transistor [package="TO92 [THT]"]
  R10 = Resistor [tolerance=±5% resistance=220 package=THT]
  J6 = female pin header, 3 pins [form="♀ (female)"]
  J_SPK1 = female pin header, 2 pins [form="♀ (female)"]
  R11 = Resistor [tolerance=±5% resistance=220 package=THT]
  J2 = female pin header, 5 pins [form="♀ (female)"]
  U1 = PCF8574 [package="DIP16 [THT]"]
  R12 = Resistor [tolerance=±5% resistance=10k package=THT]
  R13 = Resistor [tolerance=±5% resistance=10k package=THT]
  J7 = female pin header, 4 pins [form="♀ (female)"]
  R14 = Resistor [tolerance=±5% resistance=10k package=THT]
  R15 = Resistor [tolerance=±5% resistance=10k package=THT]
  R16 = Resistor [tolerance=±5% resistance=10k package=THT]
  J8 = female pin header, 3 pins [form="♀ (female)"]
  J9 = female pin header, 3 pins [form="♀ (female)"]

nets:
  N1: R6.Pin_0, Atmega2.RESET, C10.0
  VCC: R6.Pin_1, C6.1, C7.0, Atmega2.VCC, Atmega2.AVCC, Atmega2.AREF, J4.pin1, J_FTDI1.pin2, J5.pin2, Q2.C, J6.pin1, U1.VCC, R12.Pin_1, R13.Pin_1, J7.pin1, R14.Pin_1, R15.Pin_1, R16.Pin_1
  GND: S2.Pin_1, S2.Pin_2, C6.0, C7.1, C8.1, C9.1, Atmega2.GND, J4.pin2, J_FTDI1.pin1, J5.pin1, J6.pin2, J_SPK1.pin1, J2.pin1, U1.GND, J7.pin2, J8.pin1, J8.pin2, J8.pin3
  N2: S2.Pin_3, S2.Pin_4, Atmega2.PB7
  N3: R7.Pin_0, Atmega2.PB1
  N4: R7.Pin_1, J2.pin2
  N5: R8.Pin_0, Atmega2.PB2
  N6: R8.Pin_1, J2.pin3
  N7: R9.Pin_0, Atmega2.PB3
  N8: R9.Pin_1, J2.pin4
  N9: XTAL2.pin_0, C9.0, Atmega2.XTAL1
  N10: XTAL2.pin_1, C8.0, Atmega2.XTAL2
  N11: Atmega2.PB4, R11.Pin_0
  N12: Atmega2.PD0, J_FTDI1.pin3
  N13: Atmega2.PD1, J_FTDI1.pin4
  N14: Atmega2.PD5, R10.Pin_0
  N15: Atmega2.PD6, J6.pin3
  N16: Atmega2.PC0, J3.pin1, U1.SCL, R13.Pin_0, J7.pin4
  N17: Atmega2.PC1, J3.pin2, U1.SDA, R12.Pin_0, J7.pin3
  N18: J_FTDI1.pin5, C10.1
  N19: Q2.E, J_SPK1.pin2
  N20: Q2.B, R10.Pin_1
  N21: R11.Pin_1, J2.pin5
  N22: U1.A0, R16.Pin_0, J9.pin3
  N23: U1.A1, R15.Pin_0, J9.pin2
  N24: U1.A3, R14.Pin_0, J9.pin1

notes:
  SCL
  SDA
  Relay
  Spk
  LedAttivato
  LedDisattivo
  LedAnomalie
  LedMonSirena
  LCD
